# Fritzing sketch CicadaPCB (saved by Fritzing 0.9.3b)
circuit board: 9.5cm x 8.5cm

parts:
  Battery = Power plug [part_number=Battery]
  D1 = Schottky Diode [part_number=1N5824 package="300 mil [THT]"]
  D2 = Schottky Diode [part_number=1N5824 package="300 mil [THT]"]
  R1 = Resistor [tolerance=±5% resistance=1k package=THT]
  Power = Power plug [part_number=Power]
  D3 = Schottky Diode [part_number=1N5824 package="300 mil [THT]"]
  C6 = Electrolytic Capacitor [capacitance=1000µF voltage=25V part_number=680uF package="200 mil [THT, electrolytic]"]
  IRF540N = Basic FET N-Channel [part_number=IRF540N package="TO220 [THT]"]
  PC817 = Sharp PC817 [part_number=PC817 package=THT]
  R2 = Resistor [tolerance=±5% resistance=1k package=THT]
  R4 = Resistor [tolerance=±5% resistance=39k package=THT]
  R3 = Resistor [tolerance=±5% resistance=1k package=THT]
  R5 = Resistor [tolerance=±5% resistance=1k package=THT]
  R6 = Resistor [tolerance=±5% resistance=1k package=THT]
  R7 = Resistor [tolerance=±5% resistance=1k package=THT]
  S1 = Pushbutton [part_number="Enable Wizard" package="[THT]"]
  R8 = Resistor [tolerance=±5% resistance=1k package=THT]
  D5 = Schottky Diode [part_number=1N4004 package="300 mil [THT]"]
  R9 = Resistor [tolerance=±5% resistance=1k package=THT]
  R10 = Resistor [tolerance=±5% resistance=33k package=THT]
  R11 = Resistor [tolerance=±5% resistance=10k package=THT]
  R12 = Resistor [tolerance=±5% resistance=10k package=THT]
  R13 = Resistor [tolerance=±5% resistance=33k package=THT]
  DHT22 = screw terminal, 3 pins [part_number="DHT 22"]
  R14 = Resistor [tolerance=±5% resistance=1k package=THT]
  microSD1 = MicroSD Card Module
  LED1 = LED - 3mm [color="Red (633nm)" package="3 mm [THT]"]
  Pluvio = Screw terminal - 2 pins [package=THT]
  Solar_cell = Screw terminal - 2 pins [package=THT]
  C8 = Capacitor [package=cap-pth-small2]
  R = LED - 3mm [color="Red (633nm)" package="3 mm [THT]"]
  G = LED - 3mm [color="Green (555nm)" package="3 mm [THT]"]
  B = LED - 3mm [color="Blue (430nm)" package="3 mm [THT]"]
  C7 = Electrolytic Capacitor [capacitance=0.22mF part_number=220uF voltage=25V package="200 mil [THT, electrolytic]"]
  LM2596 = LM2596 [part_number=LM2596 package=TO-220F-5L]
  L1 = Inductor [package="400 mil [THT]"]
  D4 = Schottky Diode [part_number=1N5824 package="300 mil [THT]"]
  C9 = Capacitor [package=cap-pth-small2]
  ESP32_DEVKIT_04_-_38Pins = ESP32 DEVKIT 38 pins
  SIM800L = SIM800L

nets:
  battery 12v: Battery.VCC, D1.anode, R10.Pin_0
  GND: Battery.GND, Power.GND, D3.anode, C6.-, IRF540N.source, PC817.Pin_2, R4.Pin_0, R8.Pin_0, R9.Pin_0, R11.Pin_1, R12.Pin_1, DHT22.pin1, microSD1.GND, LED1.cathode, Solar_cell.pin1, C8.1, R.cathode, G.cathode, B.cathode, C7.-, LM2596.GND, LM2596.ON/OFF, C9.1, ESP32_DEVKIT_04_-_38Pins.GND
  N1: D1.cathode, D2.cathode, C6.+, LM2596.VIN
  N2: D2.anode, R1.Pin_0, Power.VCC
  N3: R1.Pin_1, LED1.anode
  N4: D3.cathode, LM2596.VOUT, L1.pin_1
  N5: IRF540N.gate, R4.Pin_1, R3.Pin_1
  N6: IRF540N.drain, SIM800L.GND
  N7: PC817.Pin_1, R2.Pin_1
  5V: PC817.Pin_4, D5.anode, DHT22.pin3, R14.Pin_0, C7.+, LM2596.FEED, L1.pin_0, D4.anode
  N8: PC817.Pin_3, R3.Pin_0
  enSIM: R2.Pin_0, ESP32_DEVKIT_04_-_38Pins.IO23
  ledRed: R5.Pin_0, ESP32_DEVKIT_04_-_38Pins.IO25
  N9: R5.Pin_1, R.anode
  ledGreen: R6.Pin_0, ESP32_DEVKIT_04_-_38Pins.IO33
  N10: R6.Pin_1, G.anode
  ledBlue: R7.Pin_0, ESP32_DEVKIT_04_-_38Pins.IO32
  N11: R7.Pin_1, B.anode
  enWiz: S1.Pin_1, S1.Pin_2, ESP32_DEVKIT_04_-_38Pins.IO26
  3v3: S1.Pin_3, S1.Pin_4, R8.Pin_1, microSD1.VCC, Pluvio.pin1, ESP32_DEVKIT_04_-_38Pins.3V3
  N12: D5.cathode, ESP32_DEVKIT_04_-_38Pins.5V
  pluvio: R9.Pin_1, Pluvio.pin2, ESP32_DEVKIT_04_-_38Pins.IO4
  voltageBattery: R10.Pin_1, R11.Pin_0, C8.2, ESP32_DEVKIT_04_-_38Pins.IO35
  voltageSolarCell: R12.Pin_0, R13.Pin_1, C9.2, ESP32_DEVKIT_04_-_38Pins.IO34
  N13: R13.Pin_0, Solar_cell.pin2
  dht22: DHT22.pin2, R14.Pin_1, ESP32_DEVKIT_04_-_38Pins.IO27
  sdMISO: microSD1.MISO, ESP32_DEVKIT_04_-_38Pins.IO18
  sdMOSI: microSD1.MOSI, ESP32_DEVKIT_04_-_38Pins.IO19
  sdSCK: microSD1.SCK, ESP32_DEVKIT_04_-_38Pins.IO22
  sdCS: microSD1.CS, ESP32_DEVKIT_04_-_38Pins.IO21
  N14: D4.cathode, SIM800L.VCC
  txSIM: ESP32_DEVKIT_04_-_38Pins.IO17, SIM800L.TXD
  rxSIM: ESP32_DEVKIT_04_-_38Pins.IO16, SIM800L.RXD

notes:
  VERSION: 0.0.1-alpha
  DATE   : 2021-01
  SITE: https://github.com/andreivo/CicadaProject
  DHT22

custom parts:
  LM2596: Regulator is a DC linear voltage regulator which can operate with a very small input–output differential voltage. The advantages of a low dropout voltage include a lower minimum operating voltage, higher efficiency operation and lower heat dissipation.
  SIM800L: SIM800L is a miniature cellular module which allows for GPRS transmission, sending and receiving SMS and making and receiving voice calls. Low cost and small footprint and quad band frequency support make this module perfect solution for any project that require long range connectivity. After connecting power module boots up, searches for cellular network and login automatically. On board LED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
