# Fritzing sketch CicadaPCBv2 (saved by Fritzing 0.9.3b)
circuit board: 9.5cm x 8.5cm

parts:
  Battery = Power plug [part_number=Battery]
  D1 = Schottky Diode [part_number=1N5824 package="300 mil [THT]"]
  D2 = Schottky Diode [part_number=1N5824 package="300 mil [THT]"]
  R1 = Resistor [tolerance=±5% resistance=1k package=THT]
  Power = Power plug [part_number=Power]
  D3 = Schottky Diode [part_number=1N5824 package="300 mil [THT]"]
  C6 = Electrolytic Capacitor [capacitance=1000µF voltage=25V part_number=680uF package="200 mil [THT, electrolytic]"]
  IRF540N = Basic FET N-Channel [part_number=IRF540N package="TO220 [THT]"]
  PC817 = Sharp PC817 [part_number=PC817 package=THT]
  R2 = Resistor [tolerance=±5% resistance=1k package=THT]
  R4 = Resistor [tolerance=±5% resistance=39k package=THT]
  R3 = Resistor [tolerance=±5% resistance=1k package=THT]
  R5 = Resistor [tolerance=±5% resistance=1k package=THT]
  R6 = Resistor [tolerance=±5% resistance=1k package=THT]
  R7 = Resistor [tolerance=±5% resistance=1k package=THT]
  S1 = Pushbutton [part_number="Enable Wizard" package="[THT]"]
  R8 = Resistor [tolerance=±5% resistance=1k package=THT]
  D5 = Schottky Diode [part_number=1N4004 package="300 mil [THT]"]
  R9 = Resistor [tolerance=±5% resistance=1k package=THT]
  R10 = Resistor [tolerance=±5% resistance=33k package=THT]
  R11 = Resistor [tolerance=±5% resistance=10k package=THT]
  R12 = Resistor [tolerance=±5% resistance=10k package=THT]
  R13 = Resistor [tolerance=±5% resistance=33k package=THT]
  DHT22 = screw terminal, 3 pins [part_number="DHT 22"]
  R14 = Resistor [tolerance=±5% resistance=1k package=THT]
  microSD = MicroSD Card Module
  LED1 = LED - 3mm [color="Red (633nm)" package="3 mm [THT]"]
  C8 = Capacitor [package=cap-pth-small2]
  R = LED - 3mm [color="Red (633nm)" package="3 mm [THT]"]
  G = LED - 3mm [color="Green (555nm)" package="3 mm [THT]"]
  B = LED - 3mm [color="Blue (430nm)" package="3 mm [THT]"]
  C7 = Electrolytic Capacitor [capacitance=0.22mF part_number=220uF voltage=25V package="200 mil [THT, electrolytic]"]
  LM2596 = LM2596 [part_number=LM2596 package=TO-220F-5L]
  L1 = Inductor [package="400 mil [THT]"]
  D4 = Schottky Diode [part_number=1N5824 package="300 mil [THT]"]
  C9 = Capacitor [package=cap-pth-small2]
  ESP32_DEVKIT_04_-_38Pins = ESP32 DEVKIT 38 pins
  SIM800L = SIM800L
  Pluvio = Screw terminal - 2 pins [package=THT]
  J1 = female pin header, 10 pins [form="♀ (female)"]
  J2 = female pin header, 10 pins [form="♀ (female)"]
  J3 = female pin header, 2 pins [form="♀ (female)"]
  2SJ306 = Basic FET P-Channel [part_number=2SJ306 package="TO220 [THT]"]
  PC818 = Sharp PC817 [part_number=PC817 package=THT]
  R15 = Resistor [tolerance=±5% resistance=1k package=THT]
  R16 = Resistor [tolerance=±5% resistance=39k package=THT]
  R17 = Resistor [tolerance=±5% resistance=1k package=THT]
  PC819 = Sharp PC817 [part_number=PC817 package=THT]
  R18 = Resistor [tolerance=±5% resistance=1k package=THT]
  R19 = Resistor [tolerance=±5% resistance=39k package=THT]
  R20 = Resistor [tolerance=±5% resistance=1k package=THT]
  2SJ306_2 = Basic FET P-Channel [part_number=2SJ306 package="TO220 [THT]"]

nets:
  battery 12v: Battery.VCC, D1.anode, PC819.Pin_4, 2SJ306_2.source
  GND: Battery.GND, Power.GND, D3.anode, C6.-, IRF540N.source, PC817.Pin_2, R4.Pin_0, R8.Pin_0, R9.Pin_0, R11.Pin_1, R12.Pin_1, DHT22.pin1, microSD.GND, LED1.cathode, C8.1, R.cathode, G.cathode, B.cathode, C7.-, LM2596.GND, LM2596.ON/OFF, C9.1, ESP32_DEVKIT_04_-_38Pins.GND, J1.pin8, J2.pin4, J2.pin7, J2.pin10, J3.pin1, PC818.Pin_2, R16.Pin_0, PC819.Pin_2, R19.Pin_0
  N1: D1.cathode, D2.cathode, C6.+, LM2596.VIN
  vcc 12v: D2.anode, R1.Pin_0, Power.VCC, 2SJ306.source, PC818.Pin_4
  N2: R1.Pin_1, LED1.anode
  N3: D3.cathode, LM2596.VOUT, L1.pin_1
  N4: IRF540N.gate, R4.Pin_1, R3.Pin_1
  N5: IRF540N.drain, SIM800L.GND
  N6: PC817.Pin_1, R2.Pin_1
  5V: PC817.Pin_4, D5.anode, DHT22.pin3, R14.Pin_0, microSD.VCC, C7.+, LM2596.FEED, L1.pin_0, D4.anode, J3.pin2
  N7: PC817.Pin_3, R3.Pin_0
  enSIM: R2.Pin_0, ESP32_DEVKIT_04_-_38Pins.IO23
  ledRed: R5.Pin_0, ESP32_DEVKIT_04_-_38Pins.IO25
  N8: R5.Pin_1, R.anode
  ledGreen: R6.Pin_0, ESP32_DEVKIT_04_-_38Pins.IO33
  N9: R6.Pin_1, G.anode
  ledBlue: R7.Pin_0, ESP32_DEVKIT_04_-_38Pins.IO32
  N10: R7.Pin_1, B.anode
  3v3: S1.Pin_1, S1.Pin_2, ESP32_DEVKIT_04_-_38Pins.3V3, Pluvio.pin1, J2.pin2
  enWiz: S1.Pin_3, S1.Pin_4, R8.Pin_1, ESP32_DEVKIT_04_-_38Pins.IO26
  5vEsp: D5.cathode, ESP32_DEVKIT_04_-_38Pins.5V, J2.pin1
  pluvio: R9.Pin_1, ESP32_DEVKIT_04_-_38Pins.IO4, Pluvio.pin2
  N11: R10.Pin_0, 2SJ306_2.drain
  voltageBattery: R10.Pin_1, R11.Pin_0, C8.2, ESP32_DEVKIT_04_-_38Pins.IO35
  voltageInputVCC: R12.Pin_0, R13.Pin_1, C9.2, ESP32_DEVKIT_04_-_38Pins.IO34
  N12: R13.Pin_0, 2SJ306.drain
  dht22: DHT22.pin2, R14.Pin_1, ESP32_DEVKIT_04_-_38Pins.IO27
  sdMISO: microSD.MISO, ESP32_DEVKIT_04_-_38Pins.IO18
  sdMOSI: microSD.MOSI, ESP32_DEVKIT_04_-_38Pins.IO19
  sdSCK: microSD.SCK, ESP32_DEVKIT_04_-_38Pins.IO22
  sdCS: microSD.CS, ESP32_DEVKIT_04_-_38Pins.IO21
  N13: D4.cathode, SIM800L.VCC
  enVoltimeter: ESP32_DEVKIT_04_-_38Pins.IO14, R17.Pin_0, R20.Pin_0
  io12: ESP32_DEVKIT_04_-_38Pins.IO12, J2.pin9
  io13: ESP32_DEVKIT_04_-_38Pins.IO13, J2.pin8
  sd2: ESP32_DEVKIT_04_-_38Pins.SD2, J2.pin6
  sd3: ESP32_DEVKIT_04_-_38Pins.SD3, J2.pin5
  CMD: ESP32_DEVKIT_04_-_38Pins.CMD, J2.pin3
  txd: ESP32_DEVKIT_04_-_38Pins.TXD0, J1.pin10
  rxd: ESP32_DEVKIT_04_-_38Pins.RXD0, J1.pin9
  io5: ESP32_DEVKIT_04_-_38Pins.IO5, J1.pin7
  txSIM: ESP32_DEVKIT_04_-_38Pins.IO17, SIM800L.TXD
  rxSIM: ESP32_DEVKIT_04_-_38Pins.IO16, SIM800L.RXD
  io0: ESP32_DEVKIT_04_-_38Pins.IO0, J1.pin6
  io2: ESP32_DEVKIT_04_-_38Pins.IO2, J1.pin5
  io15: ESP32_DEVKIT_04_-_38Pins.IO15, J1.pin4
  sd1: ESP32_DEVKIT_04_-_38Pins.SD1, J1.pin3
  sdo: ESP32_DEVKIT_04_-_38Pins.SD0, J1.pin2
  sck: ESP32_DEVKIT_04_-_38Pins.SCK, J1.pin1
  N14: 2SJ306.gate, R15.Pin_1, R16.Pin_1
  N15: PC818.Pin_1, R17.Pin_1
  N16: PC818.Pin_3, R15.Pin_0
  N17: PC819.Pin_1, R20.Pin_1
  N18: PC819.Pin_3, R18.Pin_0
  N19: R18.Pin_1, R19.Pin_1, 2SJ306_2.gate

notes:
  VERSION: 0.0.2-alpha
  DATE   : 2021-03
  https://github.com/andreivo/CicadaProject
  DHT22
  wizard
  rxd
  txd
  gnd
  io5
  io0
  io2
  io15
  sd1
  sd0
  sck
  5V
  3V3
  CMD
  GND
  sd3
  sd2
  io13
  io12
  Cicada DCP Project, Power System, 0.0.2-a
  Cicada DCP Project, Esp32, 0.0.2-a
  Cicada DCP Project, Modem, 0.0.2-a
  Cicada DCP Project, User IO, 0.0.2-a
  Cicada DCP Project, MicroSD Module, 0.0.2-a
  Cicada DCP Project, Voltimeter, 0.0.2-a
  Cicada DCP Project, Sensors, 0.0.2-a
  Cicada DCP Project, Expansion Shield, 0.0.2-a
  C6
  680uF
  25V
  C7
  220uF
  5v (3A)
  +   D   -

custom parts:
  LM2596: Regulator is a DC linear voltage regulator which can operate with a very small input–output differential voltage. The advantages of a low dropout voltage include a lower minimum operating voltage, higher efficiency operation and lower heat dissipation.
  SIM800L: SIM800L is a miniature cellular module which allows for GPRS transmission, sending and receiving SMS and making and receiving voice calls. Low cost and small footprint and quad band frequency support make this module perfect solution for any project that require long range connectivity. After connecting power module boots up, searches for cellular network and login automatically. On board LED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
